# Fritzing sketch schematic (saved by Fritzing 0.9.3b)
perfboards: 1

parts:
  WeMos_D1_Mini1 = WeMos D1 Mini
  LED_STRIP = female pin header, 4 pins [form="♀ (female)"]
  GREEN = MOSFET-NCHANNEL [part_number=TN0610 package=to-92]
  BLUE = MOSFET-NCHANNEL [part_number=TN0610 package=to-92]
  RED = MOSFET-NCHANNEL [part_number=TN0610 package=to-92]
  WPS = Pushbutton [package="[THT]"]
  IR1 = TSOP312.., 314.. [part_number=TSOP38238 package=THT]

nets:
  N1: WeMos_D1_Mini1.3V3, IR1.Vs
  N2: WeMos_D1_Mini1.5V, LED_STRIP.pin4
  N3: WeMos_D1_Mini1.D1, BLUE.G
  N4: WeMos_D1_Mini1.D2, RED.G
  N5: WeMos_D1_Mini1.D3, GREEN.G
  N6: WeMos_D1_Mini1.D5, WPS.Pin_3, WPS.Pin_4
  N7: WeMos_D1_Mini1.D6, IR1.Data
  N8: WeMos_D1_Mini1.G, GREEN.S, BLUE.S, RED.S, WPS.Pin_1, WPS.Pin_2, IR1.GND
  N9: LED_STRIP.pin1, BLUE.D
  N10: LED_STRIP.pin2, RED.D
  N11: LED_STRIP.pin3, GREEN.D

custom parts:
  MOSFET-NCHANNEL: Generic NMOS footprint
